# Fritzing sketch wiring (saved by Fritzing 0.9.3b)
circuit board: 8.46667cm x 5.64444cm
breadboards: 1

parts:
  WeMos_D1_Mini1 = WeMos D1 Mini
  Componente1 = LED Matrix - Serial Interface - Red/Green/Blue  # not connected
  Componente2 = LED Matrix - Serial Interface - Red/Green/Blue  # not connected
  Componente3 = LED Matrix - Serial Interface - Red/Green/Blue  # not connected
  Componente4 = LED Matrix - Serial Interface - Red/Green/Blue  # not connected
  R1 = Photocell (LDR) [package=THT]

nets:
  N1: WeMos_D1_Mini1.3V3, R1.pin_0
  N2: WeMos_D1_Mini1.A0, R1.pin_1
